# Fritzing sketch Platine (saved by Fritzing 0.9.9b)
circuit board: 8cm x 6.9cm
breadboards: 1

parts:
  HX711_-_2 = HX711 Weighing Sensor Module
  HX711_-1 = HX711 Weighing Sensor Module
  HX711_-_4 = HX711 Weighing Sensor Module
  HX_711_-_3 = HX711 Weighing Sensor Module
  PWR = Header 2 [package=jst-2-pth-kit]
  LED = Header 2 [package=jst-2-pth]
  D1_Mini = WeMos D1 Mini
  BT151-500R = SCR [package="TO220 [THT]"]
  R-LED = Resistor [tolerance=±5% power=0.25 resistance=220 package=THT]
  R-Gate = Resistor [tolerance=±5% power=0.25 resistance=220 package=THT]
  JP1 = Header 6 [package=1x06-smd]  # not connected
  JP2 = Header 6 [package=1x06-smd]  # not connected
  JP3 = Header 6 [package=1x06-smd]  # not connected
  JP4 = Header 6 [package=1x06-smd]  # not connected
  OPT_3_3v = SCR [package="TO220 [THT]"]
  ON = Header 2 [package=jst-2-pth]
  H1 = Header [package=THT]
  H2 = Header [package=THT]
  H3 = Header [package=THT]
  H4 = Header [package=THT]
  H5 = Header [package=THT]
  H6 = Header [package=THT]
  H7 = Header [package=THT]
  H8 = Header [package=THT]
  H9 = Header [package=THT]
  H10 = Header [package=THT]
  H11 = Header [package=THT]
  H12 = Header [package=THT]
  H13 = Header [package=THT]
  H14 = Header [package=THT]
  H15 = Header [package=THT]
  H16 = Header [package=THT]
  H17 = Header [package=THT]
  H18 = Header [package=THT]
  H19 = Header [package=THT]
  H20 = Header [package=THT]
  H21 = Header [package=THT]
  H22 = Header [package=THT]
  H23 = Header [package=THT]
  H24 = Header [package=THT]

nets:
  VCC: HX711_-_2.VCC, HX711_-1.VCC, HX711_-_4.VCC, HX_711_-_3.VCC, D1_Mini.3V3, OPT_3_3v.A
  GND: HX711_-_2.GND, HX711_-1.GND, HX711_-_4.GND, HX_711_-_3.GND, PWR.1, LED.1, D1_Mini.G, OPT_3_3v.K
  N1: HX711_-_2.DO/RX, D1_Mini.D5
  N2: HX711_-_2.CK/TX, HX711_-1.CK/TX, D1_Mini.D7
  N3: HX711_-_2.E+, H13.Pin_0
  N4: HX711_-_2.E-, H14.Pin_0
  N5: HX711_-_2.A+, H15.Pin_0
  N6: HX711_-_2.A-, H16.Pin_0
  N7: HX711_-_2.B+, H17.Pin_0
  N8: HX711_-_2.B-, H18.Pin_0
  N9: HX711_-1.DO/RX, D1_Mini.D6
  N10: HX711_-1.E+, H20.Pin_0
  N11: HX711_-1.E-, H21.Pin_0
  N12: HX711_-1.A+, H22.Pin_0
  N13: HX711_-1.A-, H19.Pin_0
  N14: HX711_-1.B+, H23.Pin_0
  N15: HX711_-1.B-, H24.Pin_0
  N16: HX711_-_4.DO/RX, D1_Mini.D1
  N17: HX711_-_4.CK/TX, HX_711_-_3.CK/TX, D1_Mini.D3
  N18: HX711_-_4.E+, H6.Pin_0
  N19: HX711_-_4.E-, H5.Pin_0
  N20: HX711_-_4.A+, H4.Pin_0
  N21: HX711_-_4.A-, H3.Pin_0
  N22: HX711_-_4.B+, H1.Pin_0
  N23: HX711_-_4.B-, H2.Pin_0
  N24: HX_711_-_3.DO/RX, D1_Mini.D2
  N25: HX_711_-_3.E+, H7.Pin_0
  N26: HX_711_-_3.E-, H8.Pin_0
  N27: HX_711_-_3.A+, H9.Pin_0
  N28: HX_711_-_3.A-, H10.Pin_0
  N29: HX_711_-_3.B+, H11.Pin_0
  N30: HX_711_-_3.B-, H12.Pin_0
  N31: PWR.2, BT151-500R.A, ON.1
  N32: LED.2, R-LED.Pin_1
  N33: D1_Mini.5V, BT151-500R.K, OPT_3_3v.G
  N34: D1_Mini.D8, R-LED.Pin_0
  N35: BT151-500R.G, R-Gate.Pin_0
  N36: R-Gate.Pin_1, ON.2

notes:
  Vitaplus/BVDG Projekt

custom parts:
  SCR: Silicon Controlled Rectifier - TO220
  Header: A generic female Header
